# Fritzing sketch TP3 (saved by Fritzing 0.9.3b)
breadboards: 1

parts:
  Componente1 = BME280 Breakout  # not connected
  hc-sr1 = hc-sr04
  LCD1 = LCD screen
  R1 = TRIMPOT [package=3362u-2]
  Mod1 = MSP-EXP432P401R_EagleCAD
  C1 = Electrolytic Capacitor [capacitance=1000μF package="1010 [SMD, electrolytic]"]

nets:
  VCC: hc-sr1.VCC, LCD1.VDD, LCD1.LED+, R1.CW, C1.+
  N1: hc-sr1.Trig, Mod1.P3.2
  N2: hc-sr1.Echo, Mod1.P3.3
  GND: hc-sr1.GND, LCD1.VSS, LCD1.R/W, LCD1.LED-, R1.CCW, C1.-
  N3: LCD1.V0, R1.WIPER
  N4: LCD1.RS, Mod1.P6.7
  N5: LCD1.E, Mod1.P6.6
  N6: LCD1.DB4, Mod1.P5.6
  N7: LCD1.DB5, Mod1.P2.4
  N8: LCD1.DB6, Mod1.P2.6
  N9: LCD1.DB7, Mod1.P2.7

custom parts:
  MSP-EXP432P401R_EagleCAD: TI Launch pad MSP-EXP432P401R development board.
